# Fritzing sketch greenhouse_schematic (saved by Fritzing 0.9.3b)
breadboards: 1

parts:
  RHT1 = Humidity and Temperature Sensor RHT03
  LDR = Photocell (LDR) [package=THT]
  R2 = Resistor [tolerance=±5% resistance=1k package="2010 [SMD]"]
  Part2 = Soil Moisture Sensor
  Water_Level_Sensor1 = Water Level Sensor
  color_sensor = TCS230 Color Sensor [part_number=101209]
  U1 = RELAY [package=relay-jzc]
  M1 = DC Motor
  U2 = RELAY [package=relay-jzc]
  IC1 = DS1307 [package=THT]
  Part3 = Arduino Mega 2560 (Rev3)

nets:
  VCC: RHT1.Vcc, LDR.pin_0, Part2.VCC, Water_Level_Sensor1.VCC, color_sensor.Vcc, IC1.X2_-_Crystal, IC1.SWQ/OUT_-_Clock_Output, Part3.5V
  N1: RHT1.Data-signal, Part3.D9_PWM
  GND: RHT1.GND_1, R2.Pin_1, Part2.GND, Water_Level_Sensor1.GND, color_sensor.Gnd, U1.COIL2, M1.pin_1, U2.COIL2, IC1.X1_-_Crystal, IC1.+V, Part3.GND
  N2: LDR.pin_1, R2.Pin_0, Part3.A0
  N3: Part2.SIG, Part3.A1
  N4: Water_Level_Sensor1.SIG, Part3.A2
  N5: color_sensor.OE, Part3.D3_PWM
  N6: color_sensor.S3, Part3.D8_PWM
  N7: color_sensor.S2, Part3.D7_PWM
  N8: U1.NO, M1.pin_2
  N9: U1.COIL1, Part3.D2_PWM
  N10: U2.COIL1, Part3.D5_PWM
  N11: IC1.Vbat_-_Backup_Supply, IC1.SCL_-_I2C_Clock, Part3.D20/SDA
  N12: IC1.0V, IC1.SDA_-_I2C_Data, Part3.D21/SCL

custom parts:
  Water Level Sensor: A water level sensor. This sensor operates at 3V to 5V. The Sig (signal) pin outputs an analogue signal that is in proportion to the amount of water in contact with the sensor.
  TCS230 Color Sensor: TCS230
